# Fritzing sketch DickJohnson (saved by Fritzing 0.8.3b)
circuit board: 16.9333cm x 5.64444cm
breadboards: 1

parts:
  Part1 = Arduino Uno (Rev3)
  R1 = Trimmer Potentiometer [maximum_resistance=10kΩ package=THT]  # not connected
  R2 = Resistor [tolerance=±5% resistance=220 package=THT]
  R3 = Resistor [tolerance=±5% resistance=220 package=THT]
  R4 = Resistor [tolerance=±5% resistance=220 package=THT]
  R5 = Resistor [tolerance=±5% resistance=220 package=THT]
  R6 = Resistor [tolerance=±5% resistance=220 package=THT]
  LED1 = LED - 3mm [color="Red (633nm)" package="3 mm [THT]"]
  LED2 = LED - 3mm [color="Red (633nm)" package="3 mm [THT]"]
  LED3 = LED - 3mm [color="Red (633nm)" package="3 mm [THT]"]
  LED4 = LED - 3mm [color="Red (633nm)" package="3 mm [THT]"]
  LED5 = LED - 3mm [color="Red (633nm)" package="3 mm [THT]"]
  J1 = Basic Servo
  C1 = Electrolytic Capacitor [capacitance=100µF package="200 mil [THT, electrolytic]"]
  S1 = Pushbutton [package="[THT]"]
  R7 = Trimmer Potentiometer [maximum_resistance=10kΩ package=THT]
  R8 = Trimmer Potentiometer [maximum_resistance=10kΩ package=THT]
  S2 = Pushbutton [package="[THT]"]

nets:
  N1: Part1.A4/SDA, R7.wiper
  N2: Part1.A5/SCL, R8.wiper
  N3: Part1.ICSP_MISO, Part1.D12/MISO, R3.Pin_0
  N4: Part1.ICSP_SCK, Part1.D13/SCK, R2.Pin_0
  N5: Part1.ICSP_MOSI, Part1.D11_PWM/MOSI, J1.pulse
  GND: Part1.GND, LED1.cathode, LED2.cathode, LED3.cathode, LED4.cathode, LED5.cathode, J1.gnd, C1.-, S1.Pin_3, S1.Pin_4, R7.leg2, R8.leg2, S2.Pin_1, S2.Pin_2
  N6: Part1.D8, R6.Pin_0
  N7: Part1.D9_PWM, R5.Pin_0
  N8: Part1.D10_PWM/SS, R4.Pin_0
  N9: Part1.D0/RX, S2.Pin_3, S2.Pin_4
  N10: Part1.D7, S1.Pin_1, S1.Pin_2
  5V: Part1.5V, J1.vcc, C1.+, R7.leg1, R8.leg1
  N11: R2.Pin_1, LED1.anode
  N12: R3.Pin_1, LED2.anode
  N13: R4.Pin_1, LED3.anode
  N14: R5.Pin_1, LED4.anode
  N15: R6.Pin_1, LED5.anode
